# Fritzing sketch system_sketch (saved by Fritzing 0.9.3b)
circuit board: 8.46667cm x 5.64444cm
perfboards: 1

parts:
  NXP_Precision_9dof = Adafruit FXOS8700 + FXAS21002 9 DoF Breakout [part_number="Adafruit #3463"]
  Arduino_Nano_v3_0 = Arduino Nano (Rev3.0)

nets:
  N1: NXP_Precision_9dof.SDA, Arduino_Nano_v3_0.A4
  N2: NXP_Precision_9dof.SCL, Arduino_Nano_v3_0.A5
  GND: NXP_Precision_9dof.GND, Arduino_Nano_v3_0.GND
  VIN: NXP_Precision_9dof.VIN, Arduino_Nano_v3_0.VIN

custom parts:
  Adafruit FXOS8700 + FXAS21002 9 DoF Breakout: The NXP Precision 9DoF breakout combines two of the best motion sensors we've tested here at Adafruit: The FXOS8700 3-Axis accelerometer and magnetometer, and the FXAS21002 3-axis gyroscope. These two sensors combine to make a nice 9-DoF kit, that can be used for motion and orientation sensing. In particular, we think this sensor set is ideal for AHRS-based orientation calculations: the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
